// Logisim project CA1_5bits.circ as structural Verilog: 1 circuit, main circuit main
module main (
  input  B4,
  input  B3,
  input  B2,
  input  B1,
  input  B0,
  input  in_6,
  output C4,
  output C3,
  output C2,
  output C1,
  output C0
);

  xor xor_1 (C4, B4, in_6);
  xor xor_2 (C3, B3, in_6);
  xor xor_3 (C2, B2, in_6);
  xor xor_4 (C0, B0, in_6);
  xor xor_5 (C1, B1, in_6);
endmodule
