// Logisim project CA2_5bits.circ as structural Verilog: 1 circuit, main circuit main
module main (
  input  B4,
  input  B3,
  input  B2,
  input  B1,
  input  B0,
  input  in_6,
  output C4,
  output C3,
  output C2,
  output C1,
  output C0
);

  wire [4:0] xor_5_out;

  xor xor_1 (xor_5_out[4], B4, in_6);
  xor xor_2 (xor_5_out[3], B3, in_6);
  xor xor_3 (xor_5_out[2], B2, in_6);
  Adder #(.width(5)) adder_1 (.a(xor_5_out), .b({5{1'b0}}), .out({C4, C3, C2, C1, C0}), .cin(1'b1));  // open: cout
  xor xor_4 (xor_5_out[1], B1, in_6);
  xor xor_5 (xor_5_out[0], B0, in_6);
endmodule
