// Logisim project Sumador_Restador_CA1_5bit.circ as structural Verilog: 1 circuit, main circuit main
module main (
  input  B4,
  input  B3,
  input  B0,
  input  in_4,
  input  A3,
  input  in_6,
  input  A0,
  input  in_8,
  input  in_9
);

  wire and_1_out, and_2_out, and_3_out, main_1_c0, main_1_c1, main_1_c2, main_1_c3, main_1_c4, main_2_c0,
       main_2_c1, main_2_c2, main_2_c3, main_2_c4, main_3_a4, main_3_out_12, main_3_s0, main_3_s1, main_3_s2,
       main_3_s3, not_1_out;

  and and_1 (and_1_out, in_9, main_3_a4);
  LED led_1 (.in(and_1_out));
  LED led_2 (.in(not_1_out));
  not not_1 (not_1_out, main_3_a4);
  CA1_5bits_main main_1 (
    .in_6(in_9), .B4(1'b0), .B3(B4), .B2(B3), .B1(B0), .B0(in_4), .C4(main_1_c4), .C3(main_1_c3),
    .C2(main_1_c2), .C1(main_1_c1), .C0(main_1_c0));
  LED led_3 (.in(main_2_c4));
  LED led_4 (.in(main_2_c3));
  LED led_5 (.in(main_2_c2));
  CA1_5bits_main main_2 (
    .in_6(and_3_out), .B4(main_3_a4), .B3(main_3_s3), .B2(main_3_s2), .B1(main_3_s1), .B0(main_3_s0),
    .C4(main_2_c4), .C3(main_2_c3), .C2(main_2_c2), .C1(main_2_c1), .C0(main_2_c0));
  LED led_6 (.in(main_2_c1));
  LED led_7 (.in(main_2_c0));
  sumador_5bits_main main_3 (
    .Cin(and_2_out), .in_6(main_1_c4), .B4(1'b0), .B3(main_1_c3), .A3(A3), .in_8(main_1_c2), .B2(in_6),
    .in_9(main_1_c1), .B1(A0), .B0(main_1_c0), .A0(in_8), .out_12(main_3_out_12), .A4(main_3_a4),
    .S3(main_3_s3), .S2(main_3_s2), .S1(main_3_s1), .S0(main_3_s0));
  and and_2 (and_2_out, in_9, main_3_out_12);
  and and_3 (and_3_out, main_3_a4, in_9);

  // Notes on the sheet:
  //   Sumador/Restador de 5 bits con Complemento a 1
  //   -
  //   signo
  //   +
  //   S4
  //   A4
  //   S0
  //   Nota: La simulación falla para resultado de resta igual a 0 por una limitación de Logisim con los bucles
endmodule
