// Logisim project Sumador_Restador_CA2_5bit.circ as structural Verilog: 1 circuit, main circuit main
module main (
  input  B4,
  input  B3,
  input  B0,
  input  in_4,
  input  A3,
  input  in_6,
  input  A0,
  input  in_8,
  input  in_9
);

  wire and_1_out, main_1_c0, main_1_c1, main_1_c2, main_1_c3, main_1_c4, main_2_c0, main_2_c1, main_2_c2,
       main_2_c3, main_2_c4, main_3_a4, main_3_s0, main_3_s1, main_3_s2, main_3_s3, main_4_a4, main_4_s0,
       main_4_s1, main_4_s2, main_4_s3, not_1_out;

  and and_1 (and_1_out, in_9, main_3_a4);
  LED led_1 (.in(and_1_out));
  LED led_2 (.in(not_1_out));
  not not_1 (not_1_out, main_3_a4);
  CA1_5bits_main main_1 (
    .in_6(in_9), .B4(1'b0), .B3(B4), .B2(B3), .B1(B0), .B0(in_4), .C4(main_1_c4), .C3(main_1_c3),
    .C2(main_1_c2), .C1(main_1_c1), .C0(main_1_c0));
  CA1_5bits_main main_2 (
    .in_6(main_3_a4), .B4(main_3_a4), .B3(main_3_s3), .B2(main_3_s2), .B1(main_3_s1), .B0(main_3_s0),
    .C4(main_2_c4), .C3(main_2_c3), .C2(main_2_c2), .C1(main_2_c1), .C0(main_2_c0));
  LED led_3 (.in(main_4_s1));
  LED led_4 (.in(main_4_s3));
  LED led_5 (.in(main_4_a4));
  LED led_6 (.in(main_4_s2));
  sumador_5bits_main main_3 (
    .Cin(in_9), .in_6(main_1_c4), .B4(1'b0), .B3(main_1_c3), .A3(A3), .in_8(main_1_c2), .B2(in_6),
    .in_9(main_1_c1), .B1(A0), .B0(main_1_c0), .A0(in_8), .A4(main_3_a4), .S3(main_3_s3), .S2(main_3_s2),
    .S1(main_3_s1), .S0(main_3_s0));  // open: out_12
  sumador_5bits_main main_4 (
    .Cin(main_3_a4), .in_6(main_2_c4), .B4(1'b0), .B3(main_2_c3), .A3(1'b0), .in_8(main_2_c2), .B2(1'b0),
    .in_9(main_2_c1), .B1(1'b0), .B0(main_2_c0), .A0(1'b0), .A4(main_4_a4), .S3(main_4_s3), .S2(main_4_s2),
    .S1(main_4_s1), .S0(main_4_s0));  // open: out_12
  LED led_7 (.in(main_4_s0));

  // Notes on the sheet:
  //   Sumador/Restador de 5 bits con Complemento a 2
  //   -
  //   signo
  //   +
  //   S4
  //   A4
  //   S0
  //   Suma 1 para convertir en Ca2
  //   Suma 1 para convertir a Ca2 si S4 = 1 (negatovo)
endmodule
