// Logisim project biestable_RS.circ as structural Verilog: 1 circuit, main circuit main
module main (
  input  R,
  input  S,
  output Q,
  output NOT_Q
);

  nor nor_1 (Q, R, NOT_Q);
  nor nor_2 (NOT_Q, Q, S);
endmodule
