// Logisim project biestable_RS_sincrono.circ as structural Verilog: 1 circuit, main circuit main
module main (
  input  R,
  input  S,
  output Q,
  output NOT_Q
);

  wire and_1_out, and_2_out, clock_1_out;

  Clock clock_1 (.out(clock_1_out));
  and and_1 (and_1_out, R, clock_1_out);
  and and_2 (and_2_out, clock_1_out, S);
  nor nor_1 (Q, and_1_out, NOT_Q);
  nor nor_2 (NOT_Q, Q, and_2_out);
endmodule
