// Logisim project booth_multiplier.circ as structural Verilog: 1 circuit, main circuit main
module main (
  input  in_1,
  input  in_2,
  input  in_3,
  input  in_4,
  input  in_5,
  input  in_6,
  input  in_7,
  input  in_8,
  input  Manual_Clock,
  input  in_10,
  output [3:0] out_11,
  output [3:0] out_12,
  output [3:0] out_13
);

  wire advanced_buzzer_1_p2, and_1_out, and_2_out, button_1_out, clock_1_out, controlled_buffer_1_out,
       not_1_out, not_2_out, not_3_out, not_4_out, not_5_out, shift_register_1_out, shift_register_2_out,
       t_ff_1_q, t_ff_1_qn, X_out;
  wire [0:0] shift_register_4_q0;
  wire [2:0] counter_1_q;
  wire [3:0] shift_register_1_q3, shift_register_2_q3, shift_register_3_q3, shift_register_5_q3;

  Clock clock_1 (.out(clock_1_out));
  Button button_1 (.out(button_1_out));
  T_Flip_Flop #(.trigger("falling")) t_ff_1 (
    .clk(and_1_out), .T(1'b1), .Q(t_ff_1_q), .Qn(t_ff_1_qn), .reset(X_out));  // open: preset, en
  assign controlled_buffer_1_out = Manual_Clock ? clock_1_out : 1'bz;  // Controlled_Buffer controlled_buffer_1
  not not_1 (not_1_out, Manual_Clock);
  assign controlled_buffer_1_out = not_1_out ? button_1_out : 1'bz;  // Controlled_Buffer controlled_buffer_2
  not not_2 (not_2_out, and_2_out);
  LED led_1 (.in(and_2_out));
  Shift_Register #(.length(4), .trigger("falling")) shift_register_1 (
    .shift(t_ff_1_q), .in(shift_register_1_q3[3]), .clk(and_1_out), .out(shift_register_1_out),
    .load(t_ff_1_qn), .clr(X_out), .d0(out_13[3]), .q0(shift_register_1_q3[3]), .d1(out_13[2]),
    .q1(shift_register_1_q3[2]), .d2(out_13[1]), .q2(shift_register_1_q3[1]), .d3(out_13[0]),
    .q3(shift_register_1_q3[0]));
  and and_1 (and_1_out, controlled_buffer_1_out, not_2_out);
  LED led_2 (.in(shift_register_1_q3[3]));
  LED led_3 (.in(shift_register_1_q3[0]));
  LED led_4 (.in(shift_register_1_q3[1]));
  LED led_5 (.in(shift_register_1_q3[2]));
  Counter #(.width(3), .max('h7)) counter_1 (
    .Q(counter_1_q), .clk(t_ff_1_qn), .clr(X_out));  // open: load, D, count, carry
  LED led_6 (.in(shift_register_2_q3[1]));
  LED led_7 (.in(shift_register_2_q3[3]));
  LED led_8 (.in(shift_register_2_q3[2]));
  LED led_9 (.in(shift_register_2_q3[0]));
  and and_2 (and_2_out, counter_1_q[2], not_4_out, not_3_out);
  not not_3 (not_3_out, counter_1_q[0]);
  not not_4 (not_4_out, counter_1_q[1]);
  Shift_Register #(.length(4), .trigger("falling")) shift_register_2 (
    .shift(t_ff_1_q), .in(shift_register_1_out), .clk(and_1_out), .out(shift_register_2_out), .load(X_out),
    .d0(shift_register_3_q3[3]), .q0(shift_register_2_q3[3]), .d1(shift_register_3_q3[2]),
    .q1(shift_register_2_q3[2]), .d2(shift_register_3_q3[1]), .q2(shift_register_2_q3[1]),
    .d3(shift_register_3_q3[0]), .q3(shift_register_2_q3[0]));  // open: clr
  Adder #(.width(4)) adder_1 (.a(shift_register_1_q3), .b(out_12), .out(out_13));  // open: cin, cout
  Multiplexer #(.select(2), .width(4), .disabled(0), .enable("false")) multiplexer_1 (
    .in0(4'b0000), .in1(shift_register_5_q3), .in2(out_11), .in3(4'b0000), .out(out_12),
    .sel({shift_register_2_q3[0], shift_register_4_q0[0]}));
  not not_5 (not_5_out, and_2_out);
  Shift_Register #(.length(4)) shift_register_3 (
    .shift(1'b0), .in(1'b0), .clk(and_1_out), .load(X_out), .d0(in_1), .q0(shift_register_3_q3[3]),
    .d1(in_2), .q1(shift_register_3_q3[2]), .d2(in_3), .q2(shift_register_3_q3[1]), .d3(in_4),
    .q3(shift_register_3_q3[0]));  // open: out, clr
  Shift_Register #(.length(1)) shift_register_4 (
    .shift(t_ff_1_q), .in(shift_register_2_out), .clk(and_1_out), .load(X_out), .clr(X_out), .d0(1'b0),
    .q0(shift_register_4_q0[0]));  // open: out
  // Advanced_buzzer advanced_buzzer_1: pin names not known; wires that end beside it: {4'b0001, shift_register_2_q3, {8{1'b0}}}, advanced_buzzer_1_p2, 7'b0100000, and_1_out
  and and_3 (advanced_buzzer_1_p2, not_5_out, in_10);
  Button X (.out(X_out));
  Shift_Register #(.length(4)) shift_register_5 (
    .shift(1'b0), .clk(and_1_out), .load(X_out), .d0(in_5), .q0(shift_register_5_q3[3]), .d1(in_6),
    .q1(shift_register_5_q3[2]), .d2(in_7), .q2(shift_register_5_q3[1]), .d3(in_8),
    .q3(shift_register_5_q3[0]));  // open: in, out, clr
  Negator #(.width(4)) negator_1 (.in(shift_register_5_q3), .out(out_11));

  // Notes on the sheet:
  //   Booth multiplier
  //   4 bits
  //   A
  //   Audio off/on
  //   Q
  //   m
  //   M
endmodule
