// Logisim project contador_3bits_tipoT.circ as structural Verilog: 1 circuit, main circuit main
module main (
  input  in_1,
  input  in_2,
  output out_3,
  output out_4,
  output out_5
);

  wire clock_1_out, controlled_buffer_1_out;

  Clock clock_1 (.out(clock_1_out));
  assign controlled_buffer_1_out = in_1 ? clock_1_out : 1'bz;  // Controlled_Buffer controlled_buffer_1
  T_Flip_Flop #(.trigger("falling")) t_ff_1 (
    .clk(controlled_buffer_1_out), .T(1'b1), .Q(out_5), .reset(in_2));  // open: Qn, preset, en
  T_Flip_Flop #(.trigger("falling")) t_ff_2 (.clk(out_5), .T(1'b1), .Q(out_4), .reset(in_2));  // open: Qn, preset, en
  T_Flip_Flop #(.trigger("falling")) t_ff_3 (.clk(out_4), .T(1'b1), .Q(out_3), .reset(in_2));  // open: Qn, preset, en
endmodule
