// Logisim project ejemplos_dmux.circ as structural Verilog: 1 circuit, main circuit main
module main (
  input  in_1,
  input  in_2,
  input  [2:0] in_3,
  input  in_4,
  output out_5,
  output out_6
);

  Multiplexer #(.select(3)) multiplexer_1 (
    .in0(1'b1), .in1(1'b0), .in2(1'b0), .in3(1'b1), .in4(1'b1), .in5(1'b0), .in6(1'b0), .in7(1'b1),
    .out(out_5), .sel({in_1, in_4, in_2}), .en(1'b1));
  Multiplexer #(.select(3)) multiplexer_2 (
    .in0(1'b1), .in1(1'b0), .in2(1'b0), .in3(1'b1), .in4(1'b1), .in5(1'b0), .in6(1'b0), .in7(1'b1),
    .out(out_6), .sel(in_3), .en(1'b1));
endmodule
