// Logisim project registro_desplazamiento_4bits_tipoD.circ as structural Verilog: 1 circuit, main circuit main
module main (
  input  Go_Reset
);

  wire and_1_out, clock_1_out, controlled_buffer_1_out, d_ff_1_q, d_ff_2_q, d_ff_3_q, not_1_out, not_2_out,
       not_3_out, random_1_out;
  wire [2:0] counter_1_q;

  Clock clock_1 (.out(clock_1_out));
  assign controlled_buffer_1_out = not_3_out ? clock_1_out : 1'bz;  // Controlled_Buffer controlled_buffer_1
  Counter #(.width(3), .max('h7)) counter_1 (
    .Q(counter_1_q), .clk(controlled_buffer_1_out), .clr(Go_Reset));  // open: load, D, count, carry
  Random #(.width(1)) random_1 (.clk(controlled_buffer_1_out), .out(random_1_out));  // open: next, clr
  not not_1 (not_1_out, counter_1_q[0]);
  not not_2 (not_2_out, counter_1_q[1]);
  not not_3 (not_3_out, and_1_out);
  and and_1 (and_1_out, not_1_out, not_2_out, counter_1_q[2]);
  D_Flip_Flop d_ff_1 (
    .clk(controlled_buffer_1_out), .D(random_1_out), .Q(d_ff_1_q), .en(not_3_out), .reset(Go_Reset));  // open: Qn, preset
  D_Flip_Flop d_ff_2 (
    .clk(controlled_buffer_1_out), .D(d_ff_1_q), .Q(d_ff_2_q), .en(not_3_out), .reset(Go_Reset));  // open: Qn, preset
  D_Flip_Flop d_ff_3 (
    .clk(controlled_buffer_1_out), .D(d_ff_2_q), .Q(d_ff_3_q), .en(not_3_out), .reset(Go_Reset));  // open: Qn, preset
  D_Flip_Flop d_ff_4 (
    .clk(controlled_buffer_1_out), .D(d_ff_3_q), .en(not_3_out), .reset(Go_Reset));  // open: Q, Qn, preset
endmodule
