// Logisim project sumador.circ as structural Verilog: 1 circuit, main circuit main
module main (
  input  C,
  input  S0,
  input  S1,
  output S,
  output C_2
);

  wire half_adder_1_out_3, half_adder_1_out_4, half_adder_2_out_4;

  Half_Adder half_adder_1 (.in_1(S0), .in_2(S1), .out_3(half_adder_1_out_3), .out_4(half_adder_1_out_4));
  Half_Adder half_adder_2 (.in_1(C), .in_2(half_adder_1_out_3), .out_3(S), .out_4(half_adder_2_out_4));
  or or_1 (C_2, half_adder_2_out_4, half_adder_1_out_4);
endmodule
