// Logisim project sumador_5bits.circ as structural Verilog: 1 circuit, main circuit main
module main (
  input  B4,
  input  A3,
  input  B2,
  input  B1,
  input  A0,
  input  in_6,
  input  B3,
  input  in_8,
  input  in_9,
  input  B0,
  input  Cin,
  output out_12,
  output A4,
  output S3,
  output S2,
  output S1,
  output S0
);

  wire main_2_c_2, main_3_c_2, main_4_c_2, main_5_c_2;

  sumador_main main_1 (.C(main_2_c_2), .S0(B4), .S1(in_6), .S(A4), .C_2(out_12));
  sumador_main main_2 (.C(main_3_c_2), .S0(A3), .S1(B3), .S(S3), .C_2(main_2_c_2));
  sumador_main main_3 (.C(main_4_c_2), .S0(B2), .S1(in_8), .S(S2), .C_2(main_3_c_2));
  sumador_main main_4 (.C(main_5_c_2), .S0(B1), .S1(in_9), .S(S1), .C_2(main_4_c_2));
  sumador_main main_5 (.C(Cin), .S0(A0), .S1(B0), .S(S0), .C_2(main_5_c_2));

  // Notes on the sheet:
  //   Cout
  //   A4
  //   A2
  //   A1
endmodule
