// Logisim project sumador_con_mux.circ as structural Verilog: 1 circuit, main circuit main
module main (
  input  Z,
  input  x,
  input  y,
  input  z_2,
  input  y_2,
  input  x_2,
  output S,
  output C,
  output S_2,
  output C_2
);

  wire half_adder_1_out_3, half_adder_1_out_4, half_adder_2_out_4, not_1_out;

  not not_1 (not_1_out, z_2);
  Half_Adder half_adder_1 (.in_1(x), .in_2(y), .out_3(half_adder_1_out_3), .out_4(half_adder_1_out_4));
  Multiplexer #(.select(2)) multiplexer_1 (
    .in0(z_2), .in1(not_1_out), .in2(not_1_out), .in3(z_2), .out(S_2), .sel({y_2, x_2}), .en(1'b1));
  Half_Adder half_adder_2 (.in_1(Z), .in_2(half_adder_1_out_3), .out_3(S), .out_4(half_adder_2_out_4));
  or or_1 (C, half_adder_2_out_4, half_adder_1_out_4);
  Multiplexer #(.select(2)) multiplexer_2 (
    .in0(1'b0), .in1(z_2), .in2(z_2), .in3(1'b1), .out(C_2), .sel({y_2, x_2}), .en(1'b1));
endmodule
