// Logisim project sumador_decoder.circ as structural Verilog: 1 circuit, main circuit main
module main (
  input  x,
  input  z,
  input  y,
  output C,
  output S
);

  wire decoder_1_out1, decoder_1_out2, decoder_1_out3, decoder_1_out4, decoder_1_out5, decoder_1_out6,
       decoder_1_out7;

  Decoder #(.select(3)) decoder_1 (
    .out1(decoder_1_out1), .out2(decoder_1_out2), .out3(decoder_1_out3), .out4(decoder_1_out4),
    .out5(decoder_1_out5), .out6(decoder_1_out6), .out7(decoder_1_out7), .sel({x, y, z}), .en(1'b1));  // open: out0
  or or_1 (C, decoder_1_out3, decoder_1_out5, decoder_1_out6, decoder_1_out7);
  or or_2 (S, decoder_1_out1, decoder_1_out2, decoder_1_out4, decoder_1_out7);
endmodule
