// Logisim project sumador_serie.circ as structural Verilog: 1 circuit, main circuit main
module main (
  input  in_1,
  input  in_2,
  input  in_3,
  input  in_4,
  input  in_5,
  input  in_6,
  input  in_7,
  input  in_8,
  output out_9,
  output out_10,
  output out_11,
  output out_12,
  output out_13
);

  wire main_2_c_2, main_3_c_2, main_4_c_2;

  sumador_main main_1 (.C(main_2_c_2), .S0(in_1), .S1(in_5), .S(out_10), .C_2(out_9));
  sumador_main main_2 (.C(main_3_c_2), .S0(in_2), .S1(in_6), .S(out_11), .C_2(main_2_c_2));
  sumador_main main_3 (.C(main_4_c_2), .S0(in_3), .S1(in_7), .S(out_12), .C_2(main_3_c_2));
  sumador_main main_4 (.C(1'b0), .S0(in_4), .S1(in_8), .S(out_13), .C_2(main_4_c_2));

  // Notes on the sheet:
  //   A
  //   B
  //   C
endmodule
