// Logisim project tipos_biestable.circ as structural Verilog: 1 circuit, main circuit main
module main (
  input  in_1,
  input  in_2,
  input  in_3,
  input  in_4,
  input  in_5,
  input  in_6,
  input  in_7,
  output out_8,
  output out_9,
  output out_10,
  output out_11
);

  wire clock_1_out, clock_2_out, clock_3_out, clock_4_out;

  Clock clock_1 (.out(clock_1_out));
  Clock clock_2 (.out(clock_2_out));
  S_R_Flip_Flop s_r_ff_1 (.S(in_2), .clk(clock_1_out), .R(in_4), .Q(out_9), .en(1'b1));  // open: Qn, preset, reset
  T_Flip_Flop t_ff_1 (.clk(clock_2_out), .T(in_5), .Q(out_10), .preset(in_7), .en(1'b1));  // open: Qn, reset
  Clock clock_3 (.out(clock_3_out));
  Clock clock_4 (.out(clock_4_out));
  J_K_Flip_Flop j_k_ff_1 (.J(in_1), .clk(clock_3_out), .K(in_3), .Q(out_8), .en(1'b1));  // open: Qn, preset, reset
  D_Flip_Flop d_ff_1 (.clk(clock_4_out), .D(in_6), .Q(out_11), .en(1'b1));  // open: Qn, preset, reset

  // Notes on the sheet:
  //   Tipo  R-S
  //   Tipo T, 1 niega la salida, 0 la mantiene
  //   Tipo  J-K
  //   Tipo D, la salida sigue a la entrada
endmodule
